# Fritzing sketch q1 (saved by Fritzing 1.0.5)
breadboards: 1

parts:
  Part1 = Arduino Uno (Rev3)
  S1 = Pushbutton [package="[THT]"]

nets:
  N1: Part1.GND, S1.Pin_3, S1.Pin_4
  N2: Part1.D7, S1.Pin_1, S1.Pin_2

// code stored in the sketch: q1.ino
const int buttonPin = 2;
const int ledPin = 11;


int buttonState = 0;


void setup() {
  pinMode(ledPin, OUTPUT);
  // *** ????????????? ***
  pinMode(buttonPin, INPUT_PULLUP); 
}


void loop() {
  buttonState = digitalRead(buttonPin);


  // *** ?????????? (LOW)??? (HIGH) ***
  if(buttonState == LOW){
      digitalWrite(ledPin, HIGH); // ??
  } else {
      digitalWrite(ledPin, LOW);  // ??
  }
}
