# Fritzing sketch q3 (saved by Fritzing 1.0.5)
breadboards: 1

parts:
  Part1 = Arduino Uno (Rev3)
  R2 = Rotary Potentiometer (Small) [maximum_resistance=10kΩ knob_status=50% power=0.5W package=THT]
  LED1 = LED - 5mm [color="Red (633nm)" current=0.030A package="5 mm [THT]"]
  R3 = Resistor [tolerance=±5% power=0.25W resistance=220 package=THT]

nets:
  N1: Part1.A0, R2.wiper
  N2: Part1.D9_PWM, LED1.anode
  N3: Part1.GND, R2.leg1, R3.Pin_0
  N4: Part1.5V, R2.leg2
  N5: LED1.cathode, R3.Pin_1
