# Fritzing sketch q4 (saved by Fritzing 1.0.5)
breadboards: 1

parts:
  Part1 = Arduino Uno (Rev3)
  R1 = Resistor [tolerance=±5% power=0.25W resistance=220 package=THT]
  LED1 = LED - 5mm [color="Red (633nm)" current=0.030A package="5 mm [THT]"]
  S1 = Pushbutton [package="[THT]"]

nets:
  N1: Part1.D11_PWM/MOSI, LED1.anode
  N2: Part1.GND, R1.Pin_0, S1.Pin_3, S1.Pin_4
  N3: Part1.D2, S1.Pin_1, S1.Pin_2
  N4: R1.Pin_1, LED1.cathode
