# Fritzing sketch 3 (saved by Fritzing 1.0.5)
breadboards: 1

parts:
  HC-SR04_Sensor_1 = HC-SR04 Ultrasonic Distance Sensor
  IC1 = ULN2003A [package="SO16 [SMD]"]
  Part1 = Arduino Uno (Rev3)

nets:
  VCC: HC-SR04_Sensor_1.VCC, IC1.COM_-_Common, Part1.5V
  N1: HC-SR04_Sensor_1.TRIG, Part1.D6_PWM
  N2: HC-SR04_Sensor_1.ECHO, Part1.D7
  GND: HC-SR04_Sensor_1.GND, Part1.GND
  N3: IC1.In_1, Part1.D8
  N4: IC1.In_2, Part1.D9_PWM
  N5: IC1.In_3, Part1.D10_PWM/SS
  N6: IC1.In_4, Part1.D11_PWM/MOSI
